// Digital circuit Processor.dig as structural Verilog
module Processor (
  input  clk,
  input  ReStart
);

  wire alu_1_p6, alu_1_p7, alu_1_p8, control_1_p3, control_1_p9, control_1_p10, control_1_p11, control_1_p12,
       control_1_p13, control_1_p14, imreg_1_p2, pc_1_p3, pc_1_p4, pc_1_p5, register_1_p5, register_1_p6,
       register_1_p7;
  wire [2:0] control_1_p8;
  wire [3:0] rom_1_d, rom_1_d_2;
  wire [6:0] rom_1_d_4;
  wire [8:8] rom_1_d_3;
  wire [15:0] driver_1_out, imreg_1_p4, multiplexer_1_out, multiplexer_2_out, pc_1_p1, pc_1_p6, pc_1_p7,
       register_1_p8, register_1_p9, signext_1_p2, signext_1_p3, signext_1_p4;

  // PC pc_1: pin names not known; wires that end beside it: pc_1_p1, clk, pc_1_p3, pc_1_p4, pc_1_p5, pc_1_p6, pc_1_p7
  ROM #(.Bits(16), .Addr_Bits(16)) rom_1 (.A(pc_1_p7), .sel(1'b1), .D({rom_1_d_4, rom_1_d_3[8], rom_1_d_2, rom_1_d}));
  assign driver_1_out = control_1_p3 ? pc_1_p6 : 16'bz;  // Driver driver_1
  // Register register_1: pin names not known; wires that end beside it: driver_1_out, clk, rom_1_d, rom_1_d_2, register_1_p5, register_1_p6, register_1_p7, register_1_p8, register_1_p9
  // ImReg imreg_1: pin names not known; wires that end beside it: {rom_1_d_4, rom_1_d_3[8], rom_1_d_2, rom_1_d}, imreg_1_p2, clk, imreg_1_p4
  // Control control_1: pin names not known; wires that end beside it: rom_1_d_4, ReStart, control_1_p3, register_1_p5, imreg_1_p2, pc_1_p3, pc_1_p4, control_1_p8, control_1_p9, control_1_p10, control_1_p11, control_1_p12, control_1_p13, control_1_p14
  // Probe R0 on register_1_p6
  // SignExt signext_1: pin names not known; wires that end beside it: {rom_1_d_4, rom_1_d_3[8], rom_1_d_2, rom_1_d}, signext_1_p2, signext_1_p3, signext_1_p4
  // Probe R1 on register_1_p7
  Multiplexer #(.Selector_Bits(3), .Bits(16)) multiplexer_1 (
    .sel(control_1_p8), .in_0(register_1_p9), .in_1(imreg_1_p4), .in_2({16{1'b0}}), .in_3(16'hff),
    .in_4(16'hfff), .in_5(signext_1_p2), .in_6(signext_1_p3), .in_7(signext_1_p4), .out(multiplexer_1_out));
  Multiplexer #(.Bits(16)) multiplexer_2 (
    .sel(control_1_p9), .in_0(register_1_p8), .in_1(register_1_p9), .out(multiplexer_2_out));
  // ALU alu_1: pin names not known; wires that end beside it: multiplexer_2_out, multiplexer_1_out, control_1_p11, clk, pc_1_p1, alu_1_p6, alu_1_p7, alu_1_p8
  assign driver_1_out = control_1_p10 ? pc_1_p1 : 16'bz;  // Driver driver_2
  // Branch branch_1: pin names not known; wires that end beside it: alu_1_p6, alu_1_p7, alu_1_p8, control_1_p12, pc_1_p5
  RAMDualPort #(.Bits(16), .Addr_Bits(16)) ramdualport_1 (
    .A(pc_1_p1), .Din(register_1_p9), .str(control_1_p13), .C(clk), .ld(control_1_p14), .D(driver_1_out));

  // Notes on the sheet:
  //   clk: Hz: 10
  //   contents of rom_1 (hex, n*v repeats v):
  //   65536
  //   5130
  //   8417
  //   19680
  //   8417
  //   5367
  //   19695
  //   28162
  //   20992
  //   31744
  //   8417
  //   19693
  //   734
  //   8417
  //   32770
  //   23053
  //   15362
  //   23574
  //   8193
  //   8417
  //   19680
  //   8417
  //   5624
  //   19695
  //   28657
  //   65535
  //   22992
  //   32770
  //   23053
  //   8194
  //   8417
  //   19680
  //   8417
  //   32804
  //   4848
  //   19695
  //   28645
  //   65535
  //   23325
  //   1025
  //   749
  //   20190
  //   6369
  //   20222
  //   6370
  //   27151
  //   16
endmodule
